// Logisim project VendingMachine.circ as structural Verilog: 4 circuits, main circuit FSM
module CoinAccumulator (
  input  Reset,
  input  Clk,
  input  State_Q1,
  input  State_Q0,
  input  C1,
  input  C0,
  output [3:0] Total,
  output out_8,
  output out_9,
  output out_10,
  output out_11
);

  wire not_1_out, not_2_out, not_3_out;
  wire [2:0] ValidCoin_out;
  wire [3:0] adder_1_out, multiplexer_1_out, multiplexer_2_out;

  Clock clock_1 ();  // open: out
  and IsReturn (out_9, State_Q1, State_Q0);
  not not_1 (not_1_out, State_Q1);
  not not_2 (not_2_out, State_Q0);
  xor ValidCoin (ValidCoin_out[0], C1, C0);
  and and_1 (ValidCoin_out[2], C1, not_3_out);
  not not_3 (not_3_out, C0);
  or ClearTotal (out_8, Reset, out_9);
  and idle (out_10, not_1_out, not_2_out);
  Register #(.width(4)) CT (.D(multiplexer_2_out), .en(1'b1), .clk(Clk), .Q(Total), .clr(out_8));
  and AddCoin (out_11, out_10, ValidCoin_out[0]);
  // Probe on {1'b0, ValidCoin_out[2], 1'b0, ValidCoin_out[0]}
  Adder #(.width(4)) adder_1 (
    .a(Total), .b({1'b0, ValidCoin_out[2], 1'b0, ValidCoin_out[0]}), .out(adder_1_out));  // open: cin, cout
  Multiplexer #(.width(4)) multiplexer_1 (.in0(Total), .in1(adder_1_out), .out(multiplexer_1_out), .sel(out_11));
  Multiplexer #(.width(4)) multiplexer_2 (.in0(multiplexer_1_out), .in1(4'b1111), .out(multiplexer_2_out), .sel(out_8));
endmodule

module PriceLookup (
  input  S1,
  input  S0,
  output [3:0] Price
);

  Multiplexer #(.select(2), .width(4)) multiplexer_1 (
    .in0(4'b0000), .in1(4'b0010), .in2(4'b0011), .in3(4'b0101), .out(Price), .sel({S1, S0}));
endmodule

module Comparatorr (
  input  [3:0] Total,
  input  [3:0] Price,
  output B
);

  wire comparator_1_eq, comparator_1_gt;

  Comparator #(.width(4)) comparator_1 (.a(Total), .b(Price), .gt(comparator_1_gt), .eq(comparator_1_eq));  // open: lt
  or or_1 (B, comparator_1_gt, comparator_1_eq);
endmodule

module FSM (
  input  S1,
  input  S0,
  input  CLOCK,
  input  RESET,
  input  C1,
  input  C0,
  output out_7,
  output out_8,
  output out_9,
  output out_10,
  output out_11
);

  wire D0_1_out, D0_2_out, D1_1_out, D1_2_out, In_check_out, IN_dispense_out, not_1_out, not_2_out,
       not_3_out, or_1_out, or_2_out, Q0_q, Q0_qn, Q1_q, Q1_qn, ValidCoin_out;
  wire [3:0] coinaccumulator_1_total, pricelookup_1_price;

  and D_milo (out_9, IN_dispense_out, not_1_out, S0);
  and D_100Plus (out_10, IN_dispense_out, S1, not_2_out);
  and D_chips (out_11, IN_dispense_out, S1, S0);
  not not_1 (not_1_out, S1);
  not not_2 (not_2_out, S0);
  and IN_dispense (IN_dispense_out, Q1_q, Q0_qn);
  and In_check (In_check_out, Q1_qn, Q0_q);
  // AND_Gate In_return has open pins: in0=Q1_q, in1=Q0_q, out=open
  CoinAccumulator coinaccumulator_1 (
    .Reset(RESET), .Clk(CLOCK), .State_Q1(Q1_q), .State_Q0(Q0_q), .C1(C1), .C0(C0),
    .Total(coinaccumulator_1_total));  // open: out_8, out_9, out_10, out_11
  PriceLookup pricelookup_1 (.S1(S1), .S0(S0), .Price(pricelookup_1_price));
  // Probe on coinaccumulator_1_total
  D_Flip_Flop Q1 (.D(or_1_out), .clk(CLOCK), .Q(Q1_q), .Qn(Q1_qn), .reset(RESET));  // open: preset
  or or_1 (or_1_out, D1_1_out, D1_2_out);
  and D1_1 (D1_1_out, Q1_q, Q0_qn);
  // Probe on pricelookup_1_price
  and D1_2 (D1_2_out, Q1_qn, Q0_q, out_8);
  xor ValidCoin (ValidCoin_out, C1, C0);
  and D0_1 (D0_1_out, Q1_q, Q0_qn);
  D_Flip_Flop Q0 (.D(or_2_out), .clk(CLOCK), .Q(Q0_q), .Qn(Q0_qn), .reset(RESET));  // open: preset
  and D0_2 (D0_2_out, Q1_qn, Q0_qn, ValidCoin_out);
  or or_2 (or_2_out, D0_1_out, D0_2_out);
  not not_3 (not_3_out, out_8);
  Comparatorr comparatorr_1 (.Total(coinaccumulator_1_total), .Price(pricelookup_1_price), .B(out_8));
  and LED_INSUF (out_7, not_3_out, In_check_out);

  // Notes on the sheet:
  //   ITEM
  //   MILO
  //   100PLUS
  //   CHIPS
  //   PRICE  S1  S0
  //   RM2
  //   0
  //   RM3
  //   1
  //   RM5
  //   1
  //   1
  //   0
  //   1
  //   TOTAL
  //   COIN
  //   PRICE
  //   C1 C0
  //   RM1   0   1 
  //   RM5    1   0
  //   B
  //   STATE 
  //   IDLE
  //   CHECK
  //   DISPENSE
  //   RETURN_CHG
  //   CODE
  //   00
  //   01
  //   10
  //   11
endmodule
